# Fritzing sketch traffic-light-board (saved by Fritzing 0.9.3b)
perfboards: 1

parts:
  J2 = male pin header, 4 pins [form="♂ (male)"]
  J1 = female pin header, 15 pins [form="♀ (female)"]
  J3 = female pin header, 15 pins [form="♀ (female)"]
  U2 = NodeMCU V3.0

nets:
  N1: J2.pin1, J1.pin14
  N2: J2.pin2, J3.pin8
  N3: J2.pin3, J3.pin7
  N4: J2.pin4, J1.pin13
  N5: U2.GND#6, U2.GND#13, U2.GND#16, U2.GND#33

notes:
  D6 D5
  VU GND
  GND
  D5
  D6
  VU

custom parts:
  NodeMCU V3.0: ESP8266 based NodeMCU
